# Fritzing sketch ckt_diagram (saved by Fritzing 0.8.7b)
breadboards: 1

parts:
  Part1 = Arduino Nano (Rev3.0) (ICSP)
  U1 = LCD-16X2 [package=lcd-16x2]
  Part2 = Bluetooth HC-05 Macho  # not connected
  S1 = SWITCH-MOMENTARY-2 [package=tactile_switch_smd-2]
  R1 = Resistor [tolerance=±5% resistance=220 package=THT]
  R2 = Resistor [tolerance=±5% resistance=220 package=THT]
  R3 = Trimmer Potentiometer [maximum_resistance=10kΩ package=THT]
  U2 = Voltage Regulator - 5V [package="DPak [SMD]"]
  VCC1 = Battery block 9V

nets:
  N1: Part1.GND, R1.Pin_1, R3.leg2
  N2: Part1.D2, U1.DB7
  N3: Part1.D3, U1.DB6
  N4: Part1.D4, U1.DB5
  N5: Part1.D5, U1.DB4
  N6: Part1.D6, R1.Pin_0
  N7: Part1.D11/MOSI, U1.E
  N8: Part1.D12/MISO, U1.RS
  N9: Part1.VIN, S1.1, R3.leg1
  VSS: U1.VSS, U1.R_W, U1.K, U2.GND, VCC1.-
  N10: U1.VDD, R2.Pin_0, U2.output_voltage
  N11: U1.VO, R3.wiper
  N12: U1.A, R2.Pin_1

notes:
  220ohms
  1k ohms
  pot-10k ohms
